# Fritzing sketch rampart3 (saved by Fritzing 1.0.4)
circuit board: 8.80001cm x 6.50001cm
breadboards: 2

parts:
  10k = Rotary Potentiometer (Small) [maximum_resistance=100kΩ knob_status=50% power=0.5W package=THT]
  10k_2 = Rotary Potentiometer (Small) [maximum_resistance=100kΩ knob_status=50% power=0.5W package=THT]
  10k_3 = Rotary Potentiometer (Small) [maximum_resistance=100kΩ knob_status=50% power=0.5W package=THT]
  S3 = Pushbutton [package="[THT]"]
  S2 = Pushbutton [package="[THT]"]
  JGND = female pin header, 4 pins [form="♀ (female)"]
  J+ = female pin header, 4 pins [form="♀ (female)"]
  1K = Resistor [tolerance=±5% resistance=4.7k power=0.25W package=THT]
  1K_2 = Resistor [tolerance=±5% resistance=1k power=0.25W package=THT]
  1k = Resistor [tolerance=±5% resistance=1k power=0.25W package=THT]
  1k_2 = Resistor [tolerance=±5% resistance=1k power=0.25W package=THT]
  JAIN = female pin header, 2 pins [form="♀ (female)"]
  LED1 = LED - 3mm [color="Red (633nm)" current=0.030A package="3 mm [THT]"]
  4_7k = Resistor [tolerance=±5% resistance=4.7k power=0.25W package=THT]
  J11 = female pin header, 2 pins [form="♀ (female)"]
  Nano = Arduino Nano (Rev3.0)
  104 = Capacitor [package=cap-pth-5mm]
  105 = Capacitor [package=cap-pth-5mm]
  10K2 = Rotary Potentiometer (Small) [maximum_resistance=10kΩ knob_status=50% power=0.5W package=THT]
  100Ω = Resistor [tolerance=±5% power=0.25 resistance=100 package=THT]
  10K = Resistor [tolerance=±5% power=0.25 resistance=10k package=THT]
  100Ω_2 = Resistor [tolerance=±5% power=0.25 resistance=100 package=THT]
  Audio_OUt1 = Audio Jack (TRS) 3.5mm [package="PG203J [THT]"]
  clckaudio1 = Audio Jack (TRS) 3.5mm [package="PG203J [THT]"]
  1K_3 = Resistor [tolerance=±5% resistance=1k power=0.25W package=THT]
  SSD1307 = OLED Mono 0.56 inch blue or white
  J2 = female pin header, 3 pins [form="♀ (female)"]
  J5 = female pin header, 3 pins [form="♀ (female)"]
  J12 = female pin header, 2 pins [form="♀ (female)"]
  RE1 = Rotary Encoder [package=THT]
  VCC1 = 4 x AAA Battery Mount [internal_resistance=0.1Ω]
  J9 = female pin header, 2 pins [form="♀ (female)"]
  S5 = SPST Switch [package=switch-spdt_kit]
  J8/7 = female pin header, 2 pins [form="♀ (female)"]
  RXTX = female pin header, 2 pins [form="♀ (female)"]
  J13 = female pin header, 5 pins [form="♀ (female)"]
  J8/8 = female pin header, 2 pins [form="♀ (female)"]
  1uF = Electrolytic Capacitor [capacitance=1µF voltage=35V package="100 mil [THT, electrolytic]"]
  J10 = female pin header, 2 pins [form="♀ (female)"]

nets:
  GND: 10k.leg1, 10k_2.leg1, 10k_3.leg1, S3.Pin_1, S3.Pin_2, S2.Pin_1, S2.Pin_2, 1K.Pin_1, 1K_2.Pin_1, 1k.Pin_1, 1k_2.Pin_1, JAIN.pin1, 4_7k.Pin_1, Nano.GND, 104.1, 10K.Pin_1, Audio_OUt1.Sleeve, clckaudio1.Sleeve, SSD1307.GND, RE1.GND, RE1.SW-2, VCC1.-, J13.pin2, 1uF.-
  N1: 10k.wiper, Nano.A0
  V++: 10k.leg2, 10k_2.leg2, 10k_3.leg2, J+.pin1, J+.pin2, J+.pin3, J+.pin4, Nano.5V, SSD1307.VCC, J13.pin1
  N2: 10k_2.wiper, Nano.A1
  N3: 10k_3.wiper, Nano.A2
  N4: S3.Pin_3, S3.Pin_4, Nano.D3, J13.pin5
  N5: S2.Pin_3, S2.Pin_4, Nano.D2, J13.pin4
  N6: JGND.pin1, 1K.Pin_0
  N7: JGND.pin2, 1K_2.Pin_0
  N8: JGND.pin3, 1k.Pin_0
  N9: JGND.pin4, 1k_2.Pin_0
  N10: JAIN.pin2, 10K2.leg1, 1uF.+
  N11: LED1.cathode, 4_7k.Pin_0
  N12: LED1.anode, Nano.D13/SCK
  N13: J11.pin1, J11.pin2, Nano.D11/MOSI
  N14: Nano.D1/TX, 1K_3.Pin_0, RXTX.pin2
  N15: Nano.D0/RX, RXTX.pin1
  N16: Nano.D4, RE1.SW-1
  N17: Nano.D5, RE1.Pin-B
  N18: Nano.D6, RE1.Pin-A
  N19: Nano.D7, J8/7.pin2
  N20: Nano.D8, J8/7.pin1
  N21: Nano.D9, 105.1, J9.pin1, J9.pin2
  N22: Nano.D10, J10.pin1, J10.pin2
  N23: Nano.D12/MISO, J12.pin1, J12.pin2
  N24: Nano.VIN, S5.S
  N25: Nano.A7, J2.pin3, J5.pin3
  N26: Nano.A6, J2.pin2, J5.pin2
  N27: Nano.A5, SSD1307.SCL
  N28: Nano.A4, SSD1307.SDA
  N29: Nano.A3, J2.pin1, J5.pin1
  N30: 104.2, 10K2.leg2, 100Ω.Pin_1
  N31: 105.2, 10K.Pin_0, 100Ω_2.Pin_1
  N32: 10K2.wiper, 100Ω_2.Pin_0
  N33: 100Ω.Pin_0, Audio_OUt1.Ring, Audio_OUt1.Tip, clckaudio1.Ring
  N34: clckaudio1.Tip, 1K_3.Pin_1
  N35: VCC1.+, S5.P
  N36: J13.pin3, J8/8.pin1, J8/8.pin2

notes:
  rampart v3
  blueprint@poetaster.de 2024

custom parts:
  OLED Mono 0.56 inch blue or white: OLED, I2C 3.3V - 5V Blue and White text versions
  Rotary Encoder: Rotary Encoder with push button
