# Fritzing sketch rampart3_top (saved by Fritzing 1.0.2b)
circuit board: 9.47613cm x 7.31289cm
breadboards: 2

parts:
  sssgv = female pin header, 5 pins [form="♀ (female)"]
  S1 = Tactile switch 12mm [package=THT]
  S2 = Tactile switch 12mm [package=THT]
  touch = male pin header, 3 pins [form="♂ (male)"]

nets:
  N1: sssgv.pin1, touch.pin3
  N2: sssgv.pin2, S1.1, S1.2, S2.1, S2.2, touch.pin1
  N3: sssgv.pin3, touch.pin2
  N4: sssgv.pin4, S2.3, S2.4
  N5: sssgv.pin5, S1.3, S1.4

notes:
  rampart
  jlcjlcjlcjlc
  367
  +/-
  4 5 + -
  rxtx
  D 12 - 7

custom parts:
  Tactile switch 12mm: 12 mm tactile switch (push button/momentary switch) from the B3F family.
