# Fritzing sketch rampart_externaldac (saved by Fritzing 1.0.2b)
circuit board: 10cm x 5.2cm
breadboards: 1

parts:
  10k = Rotary Potentiometer (Small) [maximum_resistance=100kΩ knob_status=50% power=0.5W package=THT]
  10k_2 = Rotary Potentiometer (Small) [maximum_resistance=100kΩ knob_status=50% power=0.5W package=THT]
  10k_3 = Rotary Potentiometer (Small) [maximum_resistance=100kΩ knob_status=50% power=0.5W package=THT]
  5K = Resistor [tolerance=±5% resistance=4.7k power=0.25W package=THT]
  VinGnd = female pin header, 2 pins [form="♀ (female)"]
  Nano = Arduino Nano (Rev3.0)
  A6 = female pin header, 2 pins [form="♀ (female)"]
  A7 = female pin header, 2 pins [form="♀ (female)"]
  VS1053t = female pin header, 5 pins [form="♀ (female)"]
  VS1053b = female pin header, 5 pins [form="♀ (female)"]
  SSD1306 = OLED Mono 0.56 inch blue or white
  RE3 = Rotary Encoder Pushbutton [mn=EC12E20-24P24C-SW mpn=SRPassives package=THT]
  +Pins = female pin header, 1 pin [form="♀ (female)"]
  GndPins = female pin header, 1 pin [form="♀ (female)"]
  LNinGnd = female pin header, 2 pins [form="♀ (female)"]  # not connected
  LnInGnd = female pin header, 1 pin [form="♀ (female)"]  # not connected
  M1 = VS1053-mp3-player [package=THT]  # not connected

nets:
  ENC_C/GND: 10k.leg1, 10k_2.leg1, 10k_3.leg1, 5K.Pin_1, VinGnd.pin1, Nano.GND, VS1053t.pin2, SSD1306.GND, RE3.EncoderPinC, RE3.SwitchPin1
  N1: 10k.wiper, Nano.A0
  5V: 10k.leg2, 10k_2.leg2, 10k_3.leg2, Nano.5V, VS1053t.pin1, SSD1306.VCC, +Pins.pin1
  N2: 10k_2.wiper, Nano.A1
  N3: 10k_3.wiper, Nano.A2
  N4: 5K.Pin_0, GndPins.pin1
  N5: VinGnd.pin2, Nano.VIN
  ENC_SW: Nano.D2, RE3.SwitchPin2
  ENC_B: Nano.D3, RE3.EncoderPinB
  ENC_A: Nano.D4, RE3.EncoderPinA
  DREQ: Nano.D6, VS1053t.pin4
  XDCS: Nano.D7, VS1053b.pin5
  RESET: Nano.D8, VS1053b.pin4
  XCS: Nano.D9, VS1053t.pin5
  MOSI: Nano.D11/MOSI, VS1053t.pin3
  MISO: Nano.D12/MISO, VS1053b.pin2
  N6: Nano.A7, A7.pin1, A7.pin2
  N7: Nano.A6, A6.pin1, A6.pin2
  SCL: Nano.A5, SSD1306.SCL
  SDA: Nano.A4, SSD1306.SDA
  SCK: Nano.D13/SCK, VS1053b.pin3

notes:
  rampart v1
  VS1053 stacked header representation

custom parts:
  OLED Mono 0.56 inch blue or white: OLED, I2C 3.3V - 5V Blue and White text versions
  Rotary Encoder Pushbutton: Rotary Encoder with pushbutton from SRPassives part EC12E20-24P24C-SW.
  VS1053-mp3-player: LC Technology VS1003/1053 MP3 Codec module.
