# Fritzing sketch rampart_pico_top (saved by Fritzing 1.0.6)
circuit board: 8.76236cm x 6.43364cm
breadboards: 2

parts:
  J13 = female pin header, 7 pins [form="♀ (female)"]
  J14 = female pin header, 6 pins [form="♀ (female)"]
  Touch1 = TOUCH [package=touch1]
  Touch2 = TOUCH [package=touch1]

nets:
  N1: J13.pin1, J14.pin6, Touch1.T2, Touch2.T2
  N2: J13.pin2, J14.pin5
  N3: J13.pin3, J14.pin1
  N4: J13.pin4, J14.pin3
  N5: J13.pin5, J14.pin4
  N6: J13.pin6, Touch1.T1
  N7: J13.pin7, Touch2.T1

notes:
  II
  rampart
  tx rx ~
  ~/-
  -/+
  CV
  1 2 3
  4 +
  A
  B
  C
  M
  V
